// Logisim project xkucharm1.circ as structural Verilog: 1 circuit, main circuit main
module main (
  input  A,
  input  B,
  input  C,
  input  D,
  output Y,
  output Z
);

  wire and_1_out, and_2_out, not_1_out;

  and and_1 (and_1_out, A, B);
  not not_1 (not_1_out, A);
  and and_2 (and_2_out, C, not_1_out);
  nand nand_1 (Y, and_1_out, and_2_out);
  nand nand_2 (Z, and_2_out, D);

  // Notes on the sheet:
  //   Zadanie 1 Uloha 4
  //   xkucharm1@stuba.sk
endmodule
