// Logisim project xkucharm1.circ as structural Verilog: 1 circuit, main circuit main
module main (
  input  a,
  input  b,
  input  c,
  input  d,
  output A_2,
  output B_2,
  output C_2,
  output D_2
);

  wire nand_1_out, nand_2_out, nand_3_out, nand_4_out, nand_5_out, nand_6_out, nand_7_out, nand_8_out,
       nand_9_out, not_1_out, not_2_out, not_3_out, not_4_out;

  not not_1 (not_1_out, a);
  not not_2 (not_2_out, b);
  not not_3 (not_3_out, c);
  not not_4 (not_4_out, d);
  nand nand_1 (nand_1_out, b, c);
  nand nand_2 (nand_2_out, not_1_out, b);
  nand nand_3 (nand_3_out, b, d);
  nand nand_4 (nand_4_out, not_1_out, c);
  nand nand_5 (nand_5_out, b, c);
  nand nand_6 (nand_6_out, not_1_out, b);
  nand nand_7 (nand_7_out, a, not_4_out);
  nand nand_8 (nand_8_out, not_3_out, d);
  nand nand_9 (nand_9_out, c, not_4_out);
  nand nand_10 (A_2, nand_1_out, nand_1_out);
  nand nand_11 (B_2, nand_2_out, not_1_out);
  nand nand_12 (C_2, nand_3_out, nand_4_out, nand_5_out, nand_6_out);
  nand nand_13 (D_2, nand_7_out, nand_8_out, nand_9_out);

  // Notes on the sheet:
  //   Zadanie 2 Uloha 4
  //   xkucharm1@stuba.sk
  //   AIKEN --> Grey
endmodule
