// Logisim project Schema2.circ as structural Verilog: 1 circuit, main circuit main
module main (
  input  a,
  input  b,
  input  c,
  input  d,
  output A_2,
  output B_2,
  output C_2,
  output D_2
);

  wire nand_1_out, nand_2_out, nand_3_out, nand_4_out, not_1_out, not_2_out, not_3_out, not_4_out;

  not not_1 (not_1_out, b);
  not not_2 (not_2_out, c);
  not not_3 (not_3_out, d);
  not not_4 (not_4_out, a);
  nand nand_1 (nand_1_out, b, c);
  nand nand_2 (nand_2_out, b, not_2_out, d);
  nand nand_3 (nand_3_out, b, not_3_out);
  nand nand_4 (nand_4_out, not_1_out, c);
  nand nand_5 (A_2, not_4_out, nand_1_out, nand_2_out);
  nand nand_6 (B_2, not_4_out, nand_1_out, nand_3_out);
  nand nand_7 (C_2, not_4_out, nand_2_out, nand_4_out);

  assign D_2 = d;

  // Notes on the sheet:
  //   Schema k vzorovemu rieseniu 2. zadanie
  //   BCD8421 ---> AIKEN
endmodule
