// Logisim project xkucharm1.circ as structural Verilog: 1 circuit, main circuit main
module main (
  input  x,
  output out_2
);

  wire clock_1_out, d_ff_1_q, d_ff_1_qn, d_ff_2_q, d_ff_2_qn, d_ff_3_q, d_ff_3_qn, nand_1_out, nand_2_out,
       nand_3_out, nand_4_out, nand_5_out, nand_6_out, nand_7_out, nand_8_out, nand_9_out, nand_10_out,
       not_1_out;

  not not_1 (not_1_out, x);
  nand nand_1 (nand_1_out, d_ff_2_q, x, d_ff_3_q);
  nand nand_2 (nand_2_out, d_ff_1_q, d_ff_3_qn);
  nand nand_3 (nand_3_out, d_ff_1_qn, d_ff_2_qn, d_ff_3_q, not_1_out);
  nand nand_4 (nand_4_out, d_ff_2_q, d_ff_3_qn, x);
  nand nand_5 (nand_5_out, d_ff_1_q, x);
  nand nand_6 (nand_6_out, d_ff_1_qn, x, d_ff_3_qn);
  nand nand_7 (nand_7_out, nand_1_out, nand_2_out);
  nand nand_8 (nand_8_out, nand_3_out, nand_4_out);
  nand nand_9 (nand_9_out, nand_5_out, nand_6_out);
  Clock clock_1 (.out(clock_1_out));
  D_Flip_Flop d_ff_1 (.clk(clock_1_out), .D(nand_7_out), .Q(d_ff_1_q), .Qn(d_ff_1_qn));  // open: preset, en, reset
  D_Flip_Flop d_ff_2 (.clk(clock_1_out), .D(nand_8_out), .Q(d_ff_2_q), .Qn(d_ff_2_qn));  // open: preset, en, reset
  D_Flip_Flop d_ff_3 (.clk(clock_1_out), .D(nand_9_out), .Q(d_ff_3_q), .Qn(d_ff_3_qn));  // open: preset, en, reset
  nand nand_10 (nand_10_out, d_ff_1_q, d_ff_3_q);
  nand nand_11 (out_2, nand_10_out, nand_10_out);

  // Notes on the sheet:
  //   !z3
  //   z3
  //   !z2
  //   !z1
  //   z2
  //   z1
  //   !x
  //   Zadanie 3 Úloha 4 ( 11110)
  //   xkucharm1@stuba.sk
endmodule
